# Fritzing sketch SmartSolar (saved by Fritzing 0.9.2b)
breadboards: 1

parts:
  Raspberry_Pi1 = Raspberry Pi 2
  U4 = 2-Channel 5v Relay Shield [package=relay-2ch5v10a]
  T1 = TF750712
  JP1 = USB_MICROB_PLUG [package=micro-b-ra-th]
  J1 = Screw terminal - 2 pins [part_number="Mains Power" package=THT]
  J2 = Screw terminal - 2 pins [package=THT]
  J3 = Screw terminal - 2 pins [package=THT]
  IC1 = MCP3008 8-channel 10-bit ADC [part_number=MCP3008]
  R6 = Resistor [tolerance=±5% resistance=10k package="0805 [SMD]"]
  R10 = Resistor [tolerance=±5% resistance=10k package="0805 [SMD]"]
  R12 = Resistor [tolerance=±5% resistance=10k package="0805 [SMD]"]
  J4 = Screw terminal - 2 pins [package=THT]
  J5 = Screw terminal - 2 pins [package=THT]
  J6 = Screw terminal - 2 pins [package=THT]
  LED1 = smd LED [color="Green (570nm)" package="0603 [SMD]"]
  LED2 = smd LED [color="Red (633nm)" package="0603 [SMD]"]
  R13 = Resistor [tolerance=±5% resistance=100 package="2512 [SMD]"]
  R14 = Resistor [tolerance=±5% resistance=100 package="2512 [SMD]"]

nets:
  GND: Raspberry_Pi1.GND, U4.GND, IC1.no_name_yet#9, R6.Pin_1, R10.Pin_1, R12.Pin_1
  N1: Raspberry_Pi1.GPIO10, IC1.no_name_yet#10
  N2: Raspberry_Pi1.GPIO9, IC1.no_name_yet#11
  N3: Raspberry_Pi1.GPIO11, IC1.no_name_yet#13
  N4: Raspberry_Pi1.GPIO21, LED1.cathode
  N5: Raspberry_Pi1.GPIO20, LED2.cathode
  N6: Raspberry_Pi1.GPIO8, IC1.no_name_yet#12
  N7: Raspberry_Pi1.GPIO23, U4.IN2
  N8: Raspberry_Pi1.GPIO18, U4.IN1
  5V: Raspberry_Pi1.5V, U4.VCC, IC1.no_name_yet#15, IC1.no_name_yet#16, J4.pin1, J5.pin1, J6.pin1, R13.Pin_0, R14.Pin_0
  N9: U4.K1-In, J3.pin2
  N10: U4.K1-On, U4.K2-On, T1.pin2, J1.pin2
  N11: U4.K2-In, J2.pin2
  N12: T1.pin1, J1.pin1, J2.pin1, J3.pin1
  N13: T1.pin3, JP1.D+
  N14: T1.pin6, JP1.VCC
  N15: IC1.no_name_yet#1, R6.Pin_0, J4.pin2
  N16: IC1.no_name_yet#2, R12.Pin_0, J6.pin2
  N17: IC1.no_name_yet#3, R10.Pin_0, J5.pin2
  N18: LED1.anode, R14.Pin_1
  N19: LED2.anode, R13.Pin_1

notes:
  Mains Input
  Mains Outputs to Water Pump &
  Cylinder Element
  3 x 10K Thermister Inputs
  (roof, cylinder top & bottom)
  Transformer from mains to 5V DC @ 2 Amps
  2 Relay Module (250V @ 10 Amps)
  On board LEDs to indicate when the water pump or element is on.
  MCP3008 or MCP3208 ADC (analog to digital converter)

custom parts:
  2-Channel 5v Relay Shield: 2 Channel 5v Relay Shield w. 2x SPD-06VDC-SD-C
  TF750712: Input data --------------------------------------------------- Input voltage 240 V Frequency range 50 Hz Output data --------------------------------------------------- Output voltage 2 x 6 V Power 7.0 VA Standards and security --------------------------------------------------- Approvals AS/NZS61558.2.6 & IEC60950 Thermal fuse for fail safe operation Ambient temperature max. 40 °C Class of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
